// Logisim project alu.circ as structural Verilog: 14 circuits, main circuit main
module main (
  input  [31:0] X,
  input  [31:0] Y,
  input  [3:0] Switch,
  output Signed_Overflow,
  output Equal,
  output [31:0] Result,
  output [31:0] Result_2
);

  wire add_1_overflow, comparator_1_eq, comparator_2_eq, comparator_3_eq, comparator_4_eq, comparator_5_eq,
       comparator_6_eq, comparator_7_eq, comparator_8_eq, comparator_9_eq, comparator_10_eq,
       comparator_11_eq, comparator_12_eq, comparator_13_eq, multiplexer_16_out, sub_1_overflow;
  wire [3:0] add_1_switch_val, addu_1_switch_val, and_1_switch_val, divu_1_switch_val, multu_1_switch_val,
       or_1_switch_val, sll_1_switch_val, slt_1_switch_val, sltu_1_switch_val, sra_1_switch_val,
       srl_1_switch_val, sub_1_switch_val, subu_1_switch_val;
  wire [31:0] add_1_result, addu_1_result, and_1_result, divu_1_result, divu_1_result_2, multiplexer_1_out,
       multiplexer_2_out, multiplexer_3_out, multiplexer_4_out, multiplexer_5_out, multiplexer_6_out,
       multiplexer_7_out, multiplexer_8_out, multiplexer_9_out, multiplexer_10_out, multiplexer_11_out,
       multiplexer_12_out, multiplexer_14_out, multu_1_result, multu_1_result_2, or_1_result, sll_1_result,
       slt_1_out, sltu_1_out, sra_1_result, srl_1_result, sub_1_result, subu_1_result;

  sll sll_1 (.X(X), .Y(Y), .switch_val(sll_1_switch_val), .result(sll_1_result));
  Comparator #(.width(4)) comparator_1 (.a(sll_1_switch_val), .b(Switch), .eq(comparator_1_eq));  // open: gt, lt
  srl srl_1 (.X(X), .Y(Y), .switch_val(srl_1_switch_val), .result(srl_1_result));
  Comparator #(.width(4)) comparator_2 (.a(srl_1_switch_val), .b(Switch), .eq(comparator_2_eq));  // open: gt, lt
  sra sra_1 (.X(X), .Y(Y), .switch_val(sra_1_switch_val), .result(sra_1_result));
  Comparator #(.width(4)) comparator_3 (.a(sra_1_switch_val), .b(Switch), .eq(comparator_3_eq));  // open: gt, lt
  multu multu_1 (.X(X), .Y(Y), .switch_val(multu_1_switch_val), .result(multu_1_result), .result_2(multu_1_result_2));
  Comparator #(.width(4)) comparator_4 (.a(multu_1_switch_val), .b(Switch), .eq(comparator_4_eq));  // open: gt, lt
  divu divu_1 (.X(X), .Y(Y), .switch_val(divu_1_switch_val), .result(divu_1_result), .result_2(divu_1_result_2));
  Comparator #(.width(4)) comparator_5 (.a(divu_1_switch_val), .b(Switch), .eq(comparator_5_eq));  // open: gt, lt
  add add_1 (.X(X), .Y(Y), .switch_val(add_1_switch_val), .result(add_1_result), .overflow(add_1_overflow));
  Comparator #(.width(4)) comparator_6 (.a(add_1_switch_val), .b(Switch), .eq(comparator_6_eq));  // open: gt, lt
  addu addu_1 (.X(X), .Y(Y), .switch_val(addu_1_switch_val), .result(addu_1_result));
  Comparator #(.width(4)) comparator_7 (.a(addu_1_switch_val), .b(Switch), .eq(comparator_7_eq));  // open: gt, lt
  sub sub_1 (.switch_val(sub_1_switch_val), .X(X), .result(sub_1_result), .Y(Y), .overflow(sub_1_overflow));
  Comparator #(.width(4)) comparator_8 (.a(sub_1_switch_val), .b(Switch), .eq(comparator_8_eq));  // open: gt, lt
  subu subu_1 (.X(X), .Y(Y), .switch_val(subu_1_switch_val), .result(subu_1_result));
  Comparator #(.width(4)) comparator_9 (.a(subu_1_switch_val), .b(Switch), .eq(comparator_9_eq));  // open: gt, lt
  \and  and_1 (.X(X), .Y(Y), .switch_val(and_1_switch_val), .result(and_1_result));
  Comparator #(.width(4)) comparator_10 (.a(and_1_switch_val), .b(Switch), .eq(comparator_10_eq));  // open: gt, lt
  \or  or_1 (.X(X), .Y(Y), .switch_val(or_1_switch_val), .result(or_1_result));
  Comparator #(.width(4)) comparator_11 (.a(or_1_switch_val), .b(Switch), .eq(comparator_11_eq));  // open: gt, lt
  slt slt_1 (.X(X), .Y(Y), .switch_val(slt_1_switch_val), .out(slt_1_out));
  Comparator #(.width(4)) comparator_12 (.a(slt_1_switch_val), .b(Switch), .eq(comparator_12_eq));  // open: gt, lt
  sltu sltu_1 (.X(X), .Y(Y), .switch_val(sltu_1_switch_val), .out(sltu_1_out));
  Comparator #(.width(4)) comparator_13 (.a(sltu_1_switch_val), .b(Switch), .eq(comparator_13_eq));  // open: gt, lt
  Multiplexer #(.width(32)) multiplexer_1 (
    .in0({32{1'b0}}), .in1(sll_1_result), .out(multiplexer_1_out), .sel(comparator_1_eq));  // open: en
  Multiplexer #(.width(32)) multiplexer_2 (
    .in0(multiplexer_1_out), .in1(srl_1_result), .out(multiplexer_2_out), .sel(comparator_2_eq));  // open: en
  Multiplexer #(.width(32)) multiplexer_3 (
    .in0(multiplexer_2_out), .in1(sra_1_result), .out(multiplexer_3_out), .sel(comparator_3_eq));  // open: en
  Multiplexer #(.width(32)) multiplexer_4 (
    .in0(multiplexer_3_out), .in1(multu_1_result), .out(multiplexer_4_out), .sel(comparator_4_eq));  // open: en
  Multiplexer #(.width(32)) multiplexer_5 (
    .in0(multiplexer_4_out), .in1(divu_1_result), .out(multiplexer_5_out), .sel(comparator_5_eq));  // open: en
  Multiplexer #(.width(32)) multiplexer_6 (
    .in0(multiplexer_5_out), .in1(add_1_result), .out(multiplexer_6_out), .sel(comparator_6_eq));  // open: en
  Multiplexer #(.width(32)) multiplexer_7 (
    .in0(multiplexer_6_out), .in1(addu_1_result), .out(multiplexer_7_out), .sel(comparator_7_eq));  // open: en
  Multiplexer #(.width(32)) multiplexer_8 (
    .in0(multiplexer_7_out), .in1(sub_1_result), .out(multiplexer_8_out), .sel(comparator_8_eq));  // open: en
  Multiplexer #(.width(32)) multiplexer_9 (
    .in0(multiplexer_8_out), .in1(subu_1_result), .out(multiplexer_9_out), .sel(comparator_9_eq));  // open: en
  Multiplexer #(.width(32)) multiplexer_10 (
    .in0(multiplexer_9_out), .in1(and_1_result), .out(multiplexer_10_out), .sel(comparator_10_eq));  // open: en
  Multiplexer #(.width(32)) multiplexer_11 (
    .in0(multiplexer_10_out), .in1(or_1_result), .out(multiplexer_11_out), .sel(comparator_11_eq));  // open: en
  Multiplexer #(.width(32)) multiplexer_12 (
    .in0(multiplexer_11_out), .in1(slt_1_out), .out(multiplexer_12_out), .sel(comparator_12_eq));  // open: en
  Multiplexer #(.width(32)) multiplexer_13 (
    .in0(multiplexer_12_out), .in1(sltu_1_out), .out(Result), .sel(comparator_13_eq));  // open: en
  Multiplexer #(.width(32)) multiplexer_14 (
    .in0({32{1'b0}}), .in1(multu_1_result_2), .out(multiplexer_14_out), .sel(comparator_4_eq));  // open: en
  Multiplexer #(.width(32)) multiplexer_15 (
    .in0(multiplexer_14_out), .in1(divu_1_result_2), .out(Result_2), .sel(comparator_5_eq));  // open: en
  Multiplexer multiplexer_16 (
    .in0(1'b0), .in1(add_1_overflow), .out(multiplexer_16_out), .sel(comparator_6_eq));  // open: en
  Multiplexer multiplexer_17 (
    .in0(multiplexer_16_out), .in1(sub_1_overflow), .out(Signed_Overflow), .sel(comparator_8_eq));  // open: en
  Comparator #(.width(32)) comparator_14 (.a(X), .b(Y), .eq(Equal));  // open: gt, lt

  // Other names for the same wires on the sheet: overflow = Signed_Overflow; S[3:0] = Switch

  // Notes on the sheet:
  //   INPUTS to your circuit
  //   SLL (0)
  //   SRL (1)
  //   SRA (2)
  //   MULTU (3)
  //   DIVU (4)
  //   ADD (5)
  //   ADDU (6)
  //   SUB (7)
  //   SUBU (8)
  //   AND (9)
  //   OR (10)
  //   SLT (11)
  //   SLTU (12)
  //   Result
  //   DON'T CHANGE THE LOCATIONS OF THE INPUTS AND OUTPUTS!
  //   Result2
  //   Overflow
  //   OUTPUTS from your circuit
endmodule

module sll (
  input  [31:0] X,
  input  [31:0] Y,
  output [3:0] switch_val,
  output [31:0] result
);

  wire [4:0] bit_extender_1_out;

  Bit_Extender #(.in_width(32), .out_width(5)) bit_extender_1 (.in(Y), .out(bit_extender_1_out));
  Shifter #(.width(32)) shifter_1 (.in(X), .\dist (bit_extender_1_out), .out(result));

  assign switch_val = 4'b0000;

  // Notes on the sheet:
  //   SLL (0)
endmodule

module srl (
  input  [31:0] X,
  input  [31:0] Y,
  output [3:0] switch_val,
  output [31:0] result
);

  wire [4:0] bit_extender_1_out;

  Bit_Extender #(.in_width(32), .out_width(5)) bit_extender_1 (.in(Y), .out(bit_extender_1_out));
  Shifter #(.width(32), .shift("lr")) shifter_1 (.in(X), .\dist (bit_extender_1_out), .out(result));

  assign switch_val = 4'b0001;

  // Notes on the sheet:
  //   SRL (1)
endmodule

module sra (
  input  [31:0] X,
  input  [31:0] Y,
  output [3:0] switch_val,
  output [31:0] result
);

  wire [4:0] bit_extender_1_out;

  Bit_Extender #(.in_width(32), .out_width(5)) bit_extender_1 (.in(Y), .out(bit_extender_1_out));
  Shifter #(.width(32), .shift("ar")) shifter_1 (.in(X), .\dist (bit_extender_1_out), .out(result));

  assign switch_val = 4'b0010;

  // Notes on the sheet:
  //   SRA (2)
endmodule

module multu (
  input  [31:0] X,
  input  [31:0] Y,
  output [3:0] switch_val,
  output [31:0] result,
  output [31:0] result_2
);

  Multiplier #(.width(32)) multiplier_1 (.a(X), .b(Y), .out(result), .cout(result_2));  // open: cin

  assign switch_val = 4'b0011;

  // Notes on the sheet:
  //   MULTU (3)
endmodule

module divu (
  input  [31:0] X,
  input  [31:0] Y,
  output [3:0] switch_val,
  output [31:0] result,
  output [31:0] result_2
);

  Divider #(.width(32)) divider_1 (.a(X), .b(Y), .out(result), .rem(result_2));  // open: upper

  assign switch_val = 4'b0100;

  // Notes on the sheet:
  //   DIVU (4)
endmodule

module add (
  input  [31:0] X,
  input  [31:0] Y,
  output [3:0] switch_val,
  output [31:0] result,
  output overflow
);

  wire comparator_1_eq, comparator_2_eq, not_1_out;

  Adder #(.width(32)) adder_1 (.a(X), .b(Y), .out(result));  // open: cin, cout
  Comparator #(.width(1)) comparator_1 (.a(X[31]), .b(Y[31]), .eq(comparator_1_eq));  // open: gt, lt
  not not_1 (not_1_out, comparator_2_eq);
  Comparator #(.width(1)) comparator_2 (.a(Y[31]), .b(result[31]), .eq(comparator_2_eq));  // open: gt, lt
  Multiplexer multiplexer_1 (.in0(1'b0), .in1(not_1_out), .out(overflow), .sel(comparator_1_eq));  // open: en

  assign switch_val = 4'b0101;

  // Notes on the sheet:
  //   ADD (5)
  //   Top Result Bit
endmodule

module addu (
  input  [31:0] X,
  input  [31:0] Y,
  output [3:0] switch_val,
  output [31:0] result
);

  Adder #(.width(32)) adder_1 (.a(X), .b(Y), .out(result));  // open: cin, cout

  assign switch_val = 4'b0110;

  // Notes on the sheet:
  //   ADDU (6)
endmodule

module sub (
  input  [31:0] X,
  input  [31:0] Y,
  output [3:0] switch_val,
  output [31:0] result,
  output overflow
);

  wire comparator_1_eq, comparator_2_eq, not_1_out, not_2_out;

  Subtractor #(.width(32)) subtractor_1 (.a(X), .b(Y), .out(result));  // open: bin, bout
  not not_1 (not_1_out, Y[31]);
  Comparator #(.width(1)) comparator_1 (.a(X[31]), .b(not_1_out), .eq(comparator_1_eq));  // open: gt, lt
  Comparator #(.width(1)) comparator_2 (.a(not_1_out), .b(result[31]), .eq(comparator_2_eq));  // open: gt, lt
  Multiplexer multiplexer_1 (.in0(1'b0), .in1(not_2_out), .out(overflow), .sel(comparator_1_eq));  // open: en
  not not_2 (not_2_out, comparator_2_eq);

  assign switch_val = 4'b0111;

  // Notes on the sheet:
  //   SUB (7)
  //   Top Result Bit
endmodule

module subu (
  input  [31:0] X,
  input  [31:0] Y,
  output [3:0] switch_val,
  output [31:0] result
);

  Subtractor #(.width(32)) subtractor_1 (.a(X), .b(Y), .out(result));  // open: bin, bout

  assign switch_val = 4'b1000;

  // Notes on the sheet:
  //   SUBU (8)
endmodule

module \and  (
  input  [31:0] X,
  input  [31:0] Y,
  output [3:0] switch_val,
  output [31:0] result
);

  assign result = X & Y;  // AND_Gate and_1, 32 bits wide

  assign switch_val = 4'b1001;

  // Notes on the sheet:
  //   AND (9)
endmodule

module \or  (
  input  [31:0] X,
  input  [31:0] Y,
  output [3:0] switch_val,
  output [31:0] result
);

  assign result = X | Y;  // OR_Gate or_1, 32 bits wide

  assign switch_val = 4'b1010;

  // Notes on the sheet:
  //   OR (10)
endmodule

module slt (
  input  [31:0] X,
  input  [31:0] Y,
  output [3:0] switch_val,
  output [31:0] out
);

  wire comparator_1_lt;

  Comparator #(.width(32)) comparator_1 (.a(X), .b(Y), .lt(comparator_1_lt));  // open: gt, eq
  assign out = {{31{1'b0}}, comparator_1_lt};  // Bit_Extender bit_extender_1

  assign switch_val = 4'b1011;

  // Notes on the sheet:
  //   SLT (11)
endmodule

module sltu (
  input  [31:0] X,
  input  [31:0] Y,
  output [3:0] switch_val,
  output [31:0] out
);

  wire comparator_1_lt;

  Comparator #(.width(32), .mode("unsigned")) comparator_1 (.a(X), .b(Y), .lt(comparator_1_lt));  // open: gt, eq
  assign out = {{31{1'b0}}, comparator_1_lt};  // Bit_Extender bit_extender_1

  assign switch_val = 4'b1100;

  // Notes on the sheet:
  //   SLTU (12)
endmodule
