// Logisim project cpu.circ as structural Verilog: 18 circuits, main circuit main
module main (
  input  [31:0] INSTRUCTION,
  input  CLOCK,
  output [31:0] FETCH_ADDRESS,
  output [31:0] s0_Value,
  output [31:0] s1_Value,
  output [31:0] s2_Value,
  output [31:0] ra_Value,
  output [31:0] HI_Value,
  output [31:0] LO_Value
);

  wire branching, comparator_1_eq, comparator_2_eq, comparator_3_eq, control_1_alusrc, control_1_branch,
       control_1_jump, control_1_memtoreg, control_1_memwrite, control_1_regwrite, eq, jr_control_1_jr,
       jumping, Link, main_2_signed_overflow, mfhi_control_1_mfhi, mflo_control_1_mflo, multiplexer_19_out,
       multu_or_divu_1_multu_or_divu, not_1_out, or_1_out, or_2_out, RegDst, shift_control_1_shift_control;
  wire [2:0] control_1_opunit;
  wire [3:0] alucontrol_1_aluctr;
  wire [4:0] multiplexer_4_out, multiplexer_6_out, multiplexer_7_out, multiplexer_8_out, multiplexer_11_out,
       rs, RW;
  wire [5:0] funct, opcode;
  wire [20:6] register_1_q;
  wire [27:0] bit_extender_1_out, shifter_1_out;
  wire [31:0] adder_1_out, adder_2_out, adder_3_out, immediateextender_1_extval, main_1_read_data_1,
       main_1_read_data_2, MEM_p6, multiplexer_1_out, multiplexer_2_out, multiplexer_3_out,
       multiplexer_9_out, multiplexer_10_out, multiplexer_12_out, multiplexer_13_out, multiplexer_14_out,
       multiplexer_15_out, multiplexer_16_out, multiplexer_17_out, multiplexer_18_out, multiplexer_20_out,
       multiplexer_21_out, PC_2_q, R, R2, shamt, shifter_2_out;

  Adder #(.width(32)) adder_1 (.a(FETCH_ADDRESS), .b(32'h4), .out(adder_1_out));  // open: cin, cout
  Multiplexer #(.width(32)) multiplexer_1 (
    .in0(adder_1_out), .in1(multiplexer_9_out), .out(multiplexer_1_out), .sel(or_1_out));  // open: en
  Register #(.width(32)) PC_1 (.D(multiplexer_1_out), .Q(FETCH_ADDRESS), .clk(CLOCK));  // open: en, clr
  or or_1 (or_1_out, jumping, branching);
  Register #(.width(32)) PC_2 (.D(FETCH_ADDRESS), .Q(PC_2_q), .clk(CLOCK));  // open: en, clr
  // Probe on multiplexer_2_out
  Multiplexer #(.width(32)) multiplexer_2 (
    .in0(INSTRUCTION), .in1({32{1'b0}}), .out(multiplexer_2_out), .sel(or_1_out));  // open: en
  Register #(.width(32)) register_1 (
    .D(multiplexer_2_out), .Q({opcode, rs, register_1_q, funct}), .clk(CLOCK));  // open: en, clr
  // Probe on multiplexer_9_out
  Adder #(.width(32)) adder_2 (.a(PC_2_q), .b(32'h4), .out(adder_2_out));  // open: cin, cout
  // Probe on {opcode, rs, register_1_q, funct}
  Multiplexer #(.width(32)) multiplexer_3 (
    .in0(multiplexer_10_out), .in1(adder_2_out), .out(multiplexer_3_out), .sel(Link));  // open: en
  or or_2 (or_2_out, jumping, branching);
  assign bit_extender_1_out = {{2{1'b0}}, {rs, register_1_q, funct}};  // Bit_Extender bit_extender_1
  // Probe on rs
  // Probe on register_1_q[20:16]
  Multiplexer #(.width(5)) multiplexer_4 (
    .in0({5{1'b0}}), .in1({5{1'b1}}), .out(multiplexer_4_out), .sel(or_2_out));  // open: en
  Shifter #(.width(28)) shifter_1 (.in(bit_extender_1_out), .\dist (5'b00010), .out(shifter_1_out));
  Control control_1 (
    .OpCode(opcode), .RegDst(RegDst), .ALUSrc(control_1_alusrc), .MemToReg(control_1_memtoreg),
    .RegWrite(control_1_regwrite), .MemWrite(control_1_memwrite), .Branch(control_1_branch),
    .Jump(control_1_jump), .OPUnit(control_1_opunit), .Link(Link));
  Multiplexer #(.width(5)) multiplexer_5 (
    .in0(register_1_q[20:16]), .in1(register_1_q[15:11]), .out(RW), .sel(RegDst));  // open: en
  assign shamt = {{27{1'b0}}, register_1_q[10:6]};  // Bit_Extender bit_extender_2
  Comparator #(.width(6), .mode("unsigned")) comparator_1 (
    .a(opcode), .b(6'b101100), .eq(comparator_1_eq));  // open: gt, lt
  Multiplexer #(.width(5)) multiplexer_6 (
    .in0(RW), .in1(multiplexer_4_out), .out(multiplexer_6_out), .sel(Link));  // open: en
  shift_control shift_control_1 (.opcode(opcode), .funct(funct), .shift_control(shift_control_1_shift_control));
  Multiplexer #(.width(5)) multiplexer_7 (
    .in0(rs), .in1(register_1_q[20:16]), .out(multiplexer_7_out), .sel(shift_control_1_shift_control));  // open: en
  Multiplexer #(.width(5)) multiplexer_8 (
    .in0(multiplexer_6_out), .in1(rs), .out(multiplexer_8_out), .sel(comparator_1_eq));  // open: en
  jr_control jr_control_1 (.opcode(opcode), .funct(funct), .jr(jr_control_1_jr));
  Multiplexer #(.width(32)) multiplexer_9 (
    .in0(multiplexer_12_out), .in1(main_1_read_data_1), .out(multiplexer_9_out), .sel(jr_control_1_jr));  // open: en
  // Probe on multiplexer_11_out
  Multiplexer #(.width(32)) multiplexer_10 (
    .in0(multiplexer_16_out), .in1(immediateextender_1_extval), .out(multiplexer_10_out),
    .sel(comparator_2_eq));  // open: en
  Multiplexer #(.width(5)) multiplexer_11 (
    .in0(multiplexer_8_out), .in1({5{1'b0}}), .out(multiplexer_11_out), .sel(multu_or_divu_1_multu_or_divu));  // open: en
  or or_3 (jumping, jr_control_1_jr, control_1_jump);
  Multiplexer #(.width(32)) multiplexer_12 (
    .in0(multiplexer_15_out), .in1({adder_2_out[31:28], shifter_1_out}), .out(multiplexer_12_out),
    .sel(control_1_jump));  // open: en
  regfile_main main_1 (
    .Read_Register_1(multiplexer_7_out), .Read_Register_2(register_1_q[20:16]),
    .Write_Register(multiplexer_11_out), .Write_Data(multiplexer_3_out), .Write_Enable(control_1_regwrite),
    .Clock(CLOCK), .Read_Data_1(main_1_read_data_1), .Read_Data_2(main_1_read_data_2), .s0_Value(s0_Value),
    .s1_Value(s1_Value), .s2_Value(s2_Value), .ra_Value(ra_Value));
  ImmediateExtender immediateextender_1 (
    .ImmVal({register_1_q[15:6], funct}), .opcode(opcode), .ExtVal(immediateextender_1_extval));
  Multiplexer #(.width(32)) multiplexer_13 (
    .in0(main_1_read_data_2), .in1(immediateextender_1_extval), .out(multiplexer_13_out),
    .sel(control_1_alusrc));  // open: en
  Comparator #(.width(6), .mode("unsigned")) comparator_2 (
    .a(opcode), .b(6'b001111), .eq(comparator_2_eq));  // open: gt, lt
  // Probe on immediateextender_1_extval
  Adder #(.width(32)) adder_3 (.a(adder_2_out), .b(shifter_2_out), .out(adder_3_out));  // open: cin, cout
  Shifter #(.width(32)) shifter_2 (.in(immediateextender_1_extval), .\dist (5'b00010), .out(shifter_2_out));
  Multiplexer #(.width(32)) multiplexer_14 (
    .in0(multiplexer_13_out), .in1(shamt), .out(multiplexer_14_out), .sel(shift_control_1_shift_control));  // open: en
  // Probe on alucontrol_1_aluctr
  ALUcontrol alucontrol_1 (.OpCode_31_26(opcode), .Funct_5_0(funct), .ALUCtr(alucontrol_1_aluctr));
  Multiplexer #(.width(32)) multiplexer_15 (
    .in0(adder_2_out), .in1(adder_3_out), .out(multiplexer_15_out), .sel(branching));  // open: en
  LED led_1 (.in(main_2_signed_overflow));
  alu_main main_2 (
    .Switch(alucontrol_1_aluctr), .X(main_1_read_data_1), .Equal(eq), .Result(R),
    .Signed_Overflow(main_2_signed_overflow), .Y(multiplexer_14_out), .Result_2(R2));
  Multiplexer #(.width(32)) multiplexer_16 (
    .in0(multiplexer_20_out), .in1(HI_Value), .out(multiplexer_16_out), .sel(mfhi_control_1_mfhi));  // open: en
  mfhi_control mfhi_control_1 (.opcode(opcode), .funct(funct), .mfhi(mfhi_control_1_mfhi));
  Multiplexer #(.width(32)) multiplexer_17 (
    .in0(HI_Value), .in1(R2), .out(multiplexer_17_out), .sel(multu_or_divu_1_multu_or_divu));  // open: en
  Register #(.width(32)) HI (.D(multiplexer_17_out), .Q(HI_Value), .clk(CLOCK));  // open: en, clr
  and and_1 (branching, multiplexer_19_out, control_1_branch);
  Multiplexer #(.width(32)) multiplexer_18 (
    .in0(LO_Value), .in1(R), .out(multiplexer_18_out), .sel(multu_or_divu_1_multu_or_divu));  // open: en
  multu_or_divu multu_or_divu_1 (.funct(funct), .multu_or_divu(multu_or_divu_1_multu_or_divu), .opcode(opcode));
  Comparator #(.width(6), .mode("unsigned")) comparator_3 (
    .a(opcode), .b(6'b000101), .eq(comparator_3_eq));  // open: gt, lt
  Multiplexer multiplexer_19 (.in0(eq), .in1(not_1_out), .out(multiplexer_19_out), .sel(comparator_3_eq));  // open: en
  not not_1 (not_1_out, eq);
  Multiplexer #(.width(32)) multiplexer_20 (
    .in0(multiplexer_21_out), .in1(LO_Value), .out(multiplexer_20_out), .sel(mflo_control_1_mflo));  // open: en
  mflo_control mflo_control_1 (.opcode(opcode), .funct(funct), .mflo(mflo_control_1_mflo));
  Register #(.width(32)) LO (.D(multiplexer_18_out), .Q(LO_Value), .clk(CLOCK));  // open: en, clr
  // mem_main MEM: pin names not known; wires that end beside it: R, main_1_read_data_2, control_1_memwrite, CLOCK, control_1_opunit, MEM_p6
  Multiplexer #(.width(32)) multiplexer_21 (
    .in0(R), .in1(MEM_p6), .out(multiplexer_21_out), .sel(control_1_memtoreg));  // open: en

  // Other names for the same wires on the sheet: clk = CLOCK; fetch_addr[31:0] = FETCH_ADDRESS; HI[31:0] = HI_Value;
  //   LO[31:0] = LO_Value; ra[31:0] = ra_Value; s0[31:0] = s0_Value; s1[31:0] = s1_Value; s2[31:0] = s2_Value

  // Notes on the sheet:
  //   Output
  //   These are outputs/inputs from run.circ
  //   Inputs
  //   IF || PIPELINE || EX
  //   Jump addr ->
  //   PC+4
  //   shifts
  //   rs
  //   rt
  //   Immediate (0-15) ->
  //   <- Write Data
  //   swinc
  //   Write Register
  //   These are DEBUG/TEST outputs from your circuit.
  //   jr
  //   Top 4 of PC+4
  //   Jump ->
  //   If multu or divu, write to $0
  //   Reg Write ->
  //   ImmExt
  //   lui: data from immediate field
  //   <- Data in rs
  //   Immediate
  //   ALU Control
  //   mfhi
  //   bne
  //   Branch ->
  //   MemWrite ->
  //   MemToReg ->
  //   OpUnitCode ->
  //   ALU Result
  //   mflo
  //   If multu or divu
endmodule

module Control (
  input  [5:0] OpCode,
  output RegDst,
  output ALUSrc,
  output MemToReg,
  output RegWrite,
  output MemWrite,
  output Branch,
  output Jump,
  output [2:0] OPUnit,
  output Link
);

  wire addi_out, addiu_out, andi_out, beq_out, beqal_out, bne_out, j_out, jal_out, lb_out, lbu_out, lhwu_out,
       lui_out, lw_out, not_1_out, not_2_out, not_3_out, not_4_out, not_5_out, not_6_out, not_7_out,
       not_8_out, not_9_out, not_10_out, not_11_out, not_12_out, not_13_out, not_14_out, not_15_out,
       not_16_out, not_17_out, not_18_out, not_19_out, not_20_out, not_21_out, not_22_out, not_23_out,
       not_24_out, not_25_out, not_26_out, not_27_out, not_28_out, not_29_out, not_30_out, not_31_out,
       not_32_out, not_33_out, not_34_out, not_35_out, not_36_out, not_37_out, not_38_out, not_39_out,
       not_40_out, not_41_out, not_42_out, not_43_out, not_44_out, not_45_out, not_46_out, not_47_out,
       not_48_out, not_49_out, not_50_out, not_51_out, not_52_out, not_53_out, not_54_out, not_55_out,
       not_56_out, not_57_out, not_58_out, not_59_out, not_60_out, not_61_out, not_62_out, not_63_out,
       not_64_out, not_65_out, not_66_out, not_67_out, not_68_out, not_69_out, not_70_out, not_71_out,
       not_72_out, not_73_out, not_74_out, not_75_out, not_76_out, not_77_out, or_1_out, or_2_out, or_3_out,
       or_4_out, or_5_out, or_6_out, or_7_out, or_9_out, or_10_out, or_11_out, or_12_out, or_13_out,
       or_14_out, or_15_out, or_17_out, or_18_out, or_19_out, or_20_out, or_22_out, or_24_out, or_25_out,
       or_27_out, or_28_out, or_29_out, or_30_out, or_31_out, or_32_out, or_33_out, or_34_out, ori_out,
       sb_out, shw_out, slti_out, sw_out, swai_out;
  wire [2:0] multiplexer_1_out, multiplexer_2_out, multiplexer_3_out, multiplexer_4_out, multiplexer_5_out,
       multiplexer_6_out, multiplexer_7_out;

  not not_1 (not_1_out, OpCode[5]);
  not not_2 (not_2_out, OpCode[2]);
  not not_3 (not_3_out, OpCode[4]);
  not not_4 (not_4_out, OpCode[3]);
  and R_format (RegDst, not_1_out, not_3_out, not_4_out, not_2_out, not_5_out, not_7_out);
  not not_5 (not_5_out, OpCode[1]);
  not not_6 (not_6_out, OpCode[4]);
  not not_7 (not_7_out, OpCode[0]);
  not not_8 (not_8_out, OpCode[3]);
  not not_9 (not_9_out, OpCode[2]);
  not not_10 (not_10_out, OpCode[4]);
  not not_11 (not_11_out, OpCode[3]);
  and lw (lw_out, OpCode[5], not_6_out, not_8_out, not_9_out, OpCode[1], OpCode[0]);
  Multiplexer #(.width(3)) multiplexer_1 (
    .in0(3'b000), .in1(3'b100), .out(multiplexer_1_out), .sel(lw_out));  // open: en
  not not_12 (not_12_out, OpCode[1]);
  not not_13 (not_13_out, OpCode[2]);
  not not_14 (not_14_out, OpCode[0]);
  not not_15 (not_15_out, OpCode[3]);
  not not_16 (not_16_out, OpCode[4]);
  and lb (lb_out, OpCode[5], not_10_out, not_11_out, not_13_out, not_12_out, not_14_out);
  or or_1 (or_1_out, lb_out, lw_out);
  or or_2 (or_2_out, lb_out, lw_out);
  or or_3 (or_3_out, lb_out, lw_out);
  Multiplexer #(.width(3)) multiplexer_2 (
    .in0(multiplexer_1_out), .in1(3'b001), .out(multiplexer_2_out), .sel(lb_out));  // open: en
  not not_17 (not_17_out, OpCode[1]);
  not not_18 (not_18_out, OpCode[4]);
  not not_19 (not_19_out, OpCode[3]);
  not not_20 (not_20_out, OpCode[0]);
  and lbu (lbu_out, OpCode[5], not_16_out, not_15_out, OpCode[2], not_17_out, not_20_out);
  or or_4 (or_4_out, lbu_out, or_1_out);
  or or_5 (or_5_out, lbu_out, or_2_out);
  or or_6 (or_6_out, lbu_out, or_3_out);
  Multiplexer #(.width(3)) multiplexer_3 (
    .in0(multiplexer_2_out), .in1(3'b000), .out(multiplexer_3_out), .sel(lbu_out));  // open: en
  not not_21 (not_21_out, OpCode[1]);
  and lhwu (lhwu_out, OpCode[5], not_18_out, not_19_out, OpCode[2], not_21_out, OpCode[0]);
  or or_7 (or_7_out, lhwu_out, or_4_out);
  or or_8 (MemToReg, lhwu_out, or_5_out);
  or or_9 (or_9_out, lhwu_out, or_6_out);
  Multiplexer #(.width(3)) multiplexer_4 (
    .in0(multiplexer_3_out), .in1(3'b010), .out(multiplexer_4_out), .sel(lhwu_out));  // open: en
  not not_22 (not_22_out, OpCode[2]);
  not not_23 (not_23_out, OpCode[4]);
  and sw (sw_out, OpCode[5], not_23_out, OpCode[3], not_22_out, OpCode[1], OpCode[0]);
  Multiplexer #(.width(3)) multiplexer_5 (
    .in0(multiplexer_4_out), .in1(3'b100), .out(multiplexer_5_out), .sel(sw_out));  // open: en
  not not_24 (not_24_out, OpCode[4]);
  not not_25 (not_25_out, OpCode[1]);
  not not_26 (not_26_out, OpCode[2]);
  not not_27 (not_27_out, OpCode[0]);
  and sb (sb_out, OpCode[5], not_24_out, OpCode[3], not_26_out, not_25_out, not_27_out);
  or or_10 (or_10_out, sb_out, sw_out);
  or or_11 (or_11_out, sb_out, sw_out);
  Multiplexer #(.width(3)) multiplexer_6 (
    .in0(multiplexer_5_out), .in1(3'b000), .out(multiplexer_6_out), .sel(sb_out));  // open: en
  not not_28 (not_28_out, OpCode[1]);
  not not_29 (not_29_out, OpCode[4]);
  not not_30 (not_30_out, OpCode[2]);
  and shw (shw_out, OpCode[5], not_29_out, OpCode[3], not_30_out, not_28_out, OpCode[0]);
  or or_12 (or_12_out, shw_out, or_10_out);
  or or_13 (or_13_out, shw_out, or_11_out);
  Multiplexer #(.width(3)) multiplexer_7 (
    .in0(multiplexer_6_out), .in1(3'b010), .out(multiplexer_7_out), .sel(shw_out));  // open: en
  not not_31 (not_31_out, OpCode[4]);
  not not_32 (not_32_out, OpCode[1]);
  not not_33 (not_33_out, OpCode[0]);
  and swai (swai_out, OpCode[5], not_31_out, OpCode[3], OpCode[2], not_32_out, not_33_out);
  or or_14 (or_14_out, swai_out, or_12_out);
  or or_15 (or_15_out, RegDst, swai_out);
  or or_16 (MemWrite, swai_out, or_13_out);
  Multiplexer #(.width(3)) multiplexer_8 (
    .in0(multiplexer_7_out), .in1(3'b100), .out(OPUnit), .sel(swai_out));  // open: en
  not not_34 (not_34_out, OpCode[1]);
  not not_35 (not_35_out, OpCode[0]);
  not not_36 (not_36_out, OpCode[4]);
  not not_37 (not_37_out, OpCode[5]);
  not not_38 (not_38_out, OpCode[3]);
  and beq (beq_out, not_37_out, not_36_out, not_38_out, OpCode[2], not_34_out, not_35_out);
  not not_39 (not_39_out, OpCode[5]);
  not not_40 (not_40_out, OpCode[1]);
  not not_41 (not_41_out, OpCode[4]);
  not not_42 (not_42_out, OpCode[3]);
  and bne (bne_out, not_39_out, not_41_out, not_42_out, OpCode[2], not_40_out, OpCode[0]);
  or or_17 (or_17_out, or_7_out, or_14_out);
  or or_18 (or_18_out, or_15_out, or_9_out);
  not not_43 (not_43_out, OpCode[0]);
  not not_44 (not_44_out, OpCode[1]);
  not not_45 (not_45_out, OpCode[3]);
  not not_46 (not_46_out, OpCode[5]);
  and beqal (beqal_out, not_46_out, OpCode[4], not_45_out, OpCode[2], not_44_out, not_43_out);
  or or_19 (or_19_out, bne_out, beq_out);
  not not_47 (not_47_out, OpCode[3]);
  not not_48 (not_48_out, OpCode[4]);
  not not_49 (not_49_out, OpCode[5]);
  not not_50 (not_50_out, OpCode[2]);
  and j (j_out, not_49_out, not_48_out, not_47_out, not_50_out, OpCode[1], not_55_out);
  or or_20 (or_20_out, beqal_out, or_18_out);
  or or_21 (Branch, beqal_out, or_19_out);
  not not_51 (not_51_out, OpCode[3]);
  not not_52 (not_52_out, OpCode[2]);
  not not_53 (not_53_out, OpCode[5]);
  not not_54 (not_54_out, OpCode[4]);
  not not_55 (not_55_out, OpCode[0]);
  and jal (jal_out, not_53_out, not_54_out, not_51_out, not_52_out, OpCode[1], OpCode[0]);
  not not_56 (not_56_out, OpCode[4]);
  not not_57 (not_57_out, OpCode[5]);
  or or_22 (or_22_out, jal_out, or_20_out);
  or or_23 (Link, jal_out, beqal_out);
  not not_58 (not_58_out, OpCode[5]);
  not not_59 (not_59_out, OpCode[0]);
  not not_60 (not_60_out, OpCode[4]);
  not not_61 (not_61_out, OpCode[2]);
  not not_62 (not_62_out, OpCode[1]);
  and addi (addi_out, not_57_out, not_56_out, OpCode[3], not_61_out, not_62_out, not_59_out);
  or or_24 (or_24_out, addi_out, or_17_out);
  or or_25 (or_25_out, addi_out, or_22_out);
  or or_26 (Jump, jal_out, j_out);
  not not_63 (not_63_out, OpCode[2]);
  not not_64 (not_64_out, OpCode[4]);
  not not_65 (not_65_out, OpCode[5]);
  not not_66 (not_66_out, OpCode[1]);
  and addiu (addiu_out, not_58_out, not_60_out, OpCode[3], not_63_out, not_66_out, OpCode[0]);
  or or_27 (or_27_out, addiu_out, or_24_out);
  or or_28 (or_28_out, addiu_out, or_25_out);
  not not_67 (not_67_out, OpCode[1]);
  not not_68 (not_68_out, OpCode[0]);
  not not_69 (not_69_out, OpCode[4]);
  not not_70 (not_70_out, OpCode[5]);
  and andi (andi_out, not_65_out, not_64_out, OpCode[3], OpCode[2], not_67_out, not_68_out);
  or or_29 (or_29_out, andi_out, or_27_out);
  or or_30 (or_30_out, andi_out, or_28_out);
  not not_71 (not_71_out, OpCode[5]);
  not not_72 (not_72_out, OpCode[1]);
  not not_73 (not_73_out, OpCode[4]);
  and ori (ori_out, not_70_out, not_69_out, OpCode[3], OpCode[2], not_72_out, OpCode[0]);
  or or_31 (or_31_out, ori_out, or_29_out);
  or or_32 (or_32_out, ori_out, or_30_out);
  not not_74 (not_74_out, OpCode[4]);
  not not_75 (not_75_out, OpCode[5]);
  and lui (lui_out, not_71_out, not_73_out, OpCode[3], OpCode[2], OpCode[1], OpCode[0]);
  and slti (slti_out, not_75_out, not_74_out, OpCode[3], not_77_out, OpCode[1], not_76_out);
  or or_33 (or_33_out, lui_out, or_31_out);
  or or_34 (or_34_out, lui_out, or_32_out);
  not not_76 (not_76_out, OpCode[0]);
  not not_77 (not_77_out, OpCode[2]);
  or or_35 (ALUSrc, slti_out, or_33_out);
  or or_36 (RegWrite, slti_out, or_34_out);
  // Probe on OPUnit

  // Notes on the sheet:
  //   R-Type
  //   Loads
  //   Stores
  //   Branches
  //   Jumps
  //   I-Types
  //   Outputs
endmodule

module ALUcontrol (
  input  [5:0] OpCode_31_26,
  input  [5:0] Funct_5_0,
  output [3:0] ALUCtr
);

  wire and_1_out, not_1_out, not_2_out, not_3_out, not_4_out, not_5_out, not_6_out;
  wire [3:0] itypeop0_1_operation_0, rtypeop0_1_operation_0;

  ITypeOp3 itypeop3_1 (.in_1(OpCode_31_26), .Operation_3(itypeop0_1_operation_0[3]));
  RTypeOp3 rtypeop3_1 (.in_1(Funct_5_0), .Op3(rtypeop0_1_operation_0[3]));
  ITypeOp1 itypeop1_1 (.in_1(OpCode_31_26), .Operation_1(itypeop0_1_operation_0[1]));
  ITypeOp2 itypeop2_1 (.in_1(OpCode_31_26), .Operation_2(itypeop0_1_operation_0[2]));
  RTypeOp1 rtypeop1_1 (.in_1(Funct_5_0), .Op1(rtypeop0_1_operation_0[1]));
  RTypeOp2 rtypeop2_1 (.in_1(Funct_5_0), .Op2(rtypeop0_1_operation_0[2]));
  ITypeOp0 itypeop0_1 (.in_1(OpCode_31_26), .Operation_0(itypeop0_1_operation_0[0]));
  RTypeOp0 rtypeop0_1 (.in_1(Funct_5_0), .Operation_0(rtypeop0_1_operation_0[0]));
  not not_1 (not_1_out, OpCode_31_26[5]);
  not not_2 (not_2_out, OpCode_31_26[4]);
  not not_3 (not_3_out, OpCode_31_26[3]);
  not not_4 (not_4_out, OpCode_31_26[2]);
  not not_5 (not_5_out, OpCode_31_26[0]);
  not not_6 (not_6_out, OpCode_31_26[1]);
  and and_1 (and_1_out, not_1_out, not_2_out, not_3_out, not_4_out, not_6_out, not_5_out);
  Multiplexer #(.width(4)) multiplexer_1 (
    .in0(itypeop0_1_operation_0), .in1(rtypeop0_1_operation_0), .out(ALUCtr), .sel(and_1_out));  // open: en
  // Probe on ALUCtr
endmodule

module ALUControlBACKUP (
  input  [1:0] ALUOp,
  input  [5:0] F_5_0,
  input  [5:0] OpCode_31_26,
  input  [1:0] ALUOp_2,
  input  [5:0] Funct_5_0,
  output [3:0] ALUCtr,
  output [3:0] ALUCtr_2
);

  wire and_1_out, not_1_out, not_2_out, not_3_out, or_1_out;
  wire [3:0] itypeop0_1_operation_0, rtypeop0_1_operation_0;

  ITypeOp3 itypeop3_1 (.in_1(OpCode_31_26), .Operation_3(itypeop0_1_operation_0[3]));
  ITypeOp2 itypeop2_1 (.in_1(OpCode_31_26), .Operation_2(itypeop0_1_operation_0[2]));
  RTypeOp3 rtypeop3_1 (.in_1(Funct_5_0), .Op3(rtypeop0_1_operation_0[3]));
  RTypeOp2 rtypeop2_1 (.in_1(Funct_5_0), .Op2(rtypeop0_1_operation_0[2]));
  or or_1 (or_1_out, F_5_0[3], F_5_0[0]);
  ITypeOp1 itypeop1_1 (.in_1(OpCode_31_26), .Operation_1(itypeop0_1_operation_0[1]));
  ITypeOp0 itypeop0_1 (.in_1(OpCode_31_26), .Operation_0(itypeop0_1_operation_0[0]));
  RTypeOp0 rtypeop0_1 (.in_1(Funct_5_0), .Operation_0(rtypeop0_1_operation_0[0]));
  RTypeOp1 rtypeop1_1 (.in_1(Funct_5_0), .Op1(rtypeop0_1_operation_0[1]));
  not not_1 (not_1_out, ALUOp[0]);
  and and_1 (and_1_out, ALUOp[1], F_5_0[1]);
  not not_2 (not_2_out, ALUOp[1]);
  or or_2 (ALUCtr[1], not_2_out, not_3_out);
  not not_3 (not_3_out, F_5_0[2]);
  and and_2 (ALUCtr[0], ALUOp[1], or_1_out);
  and and_3 (ALUCtr[3], ALUOp[0], not_1_out);
  or or_3 (ALUCtr[2], ALUOp[0], and_1_out);
  Multiplexer #(.width(4)) multiplexer_1 (
    .in0(itypeop0_1_operation_0), .in1(rtypeop0_1_operation_0), .out(ALUCtr_2));  // open: sel, en
  // Probe on ALUCtr
  // Probe on ALUCtr_2

  // Notes on the sheet:
  //   ALUOp0
  //   ALUOp1
  //   Operation3
  //   Operation2
  //   Operation1
  //   Operation0
  //   ALUOp0
endmodule

module RTypeOp0 (
  input  [5:0] in_1,
  output Operation_0
);

  wire add_out, and_out, multu_out, not_1_out, not_2_out, not_3_out, not_4_out, not_5_out, not_6_out,
       not_7_out, not_8_out, not_9_out, not_10_out, not_11_out, not_12_out, not_13_out, not_14_out,
       not_15_out, not_16_out, not_17_out, not_18_out, not_19_out, not_20_out, not_21_out, not_22_out,
       not_23_out, not_24_out, slt_out, srl_out, sub_out;

  not not_1 (not_1_out, in_1[4]);
  not not_2 (not_2_out, in_1[1]);
  not not_3 (not_3_out, in_1[3]);
  not not_4 (not_4_out, in_1[2]);
  and add (add_out, in_1[5], not_1_out, not_3_out, not_4_out, not_2_out, not_6_out);
  not not_5 (not_5_out, in_1[4]);
  not not_6 (not_6_out, in_1[0]);
  not not_7 (not_7_out, in_1[1]);
  not not_8 (not_8_out, in_1[3]);
  and \and  (and_out, in_1[5], not_5_out, not_8_out, in_1[2], not_7_out, not_12_out);
  not not_9 (not_9_out, in_1[5]);
  not not_10 (not_10_out, in_1[2]);
  not not_11 (not_11_out, in_1[1]);
  not not_12 (not_12_out, in_1[0]);
  and multu (multu_out, not_9_out, in_1[4], in_1[3], not_10_out, not_11_out, in_1[0]);
  not not_13 (not_13_out, in_1[2]);
  not not_14 (not_14_out, in_1[4]);
  and slt (slt_out, in_1[5], not_14_out, in_1[3], not_13_out, in_1[1], not_17_out);
  or or_1 (Operation_0, add_out, and_out, multu_out, slt_out, srl_out, sub_out);
  not not_15 (not_15_out, in_1[2]);
  not not_16 (not_16_out, in_1[5]);
  not not_17 (not_17_out, in_1[0]);
  not not_18 (not_18_out, in_1[3]);
  not not_19 (not_19_out, in_1[4]);
  and srl (srl_out, not_16_out, not_19_out, not_18_out, not_15_out, in_1[1], not_22_out);
  not not_20 (not_20_out, in_1[4]);
  not not_21 (not_21_out, in_1[2]);
  not not_22 (not_22_out, in_1[0]);
  not not_23 (not_23_out, in_1[3]);
  and sub (sub_out, in_1[5], not_20_out, not_23_out, not_21_out, in_1[1], not_24_out);
  not not_24 (not_24_out, in_1[0]);
endmodule

module RTypeOp1 (
  input  [5:0] in_1,
  output Op1
);

  wire addu_out, multu_out, not_1_out, not_2_out, not_3_out, not_4_out, not_5_out, not_6_out, not_7_out,
       not_8_out, not_9_out, not_10_out, not_11_out, not_12_out, not_13_out, not_14_out, not_15_out,
       not_16_out, not_17_out, not_18_out, not_19_out, not_20_out, not_21_out, or_out, slt_out, sra_out,
       sub_out;

  not not_1 (not_1_out, in_1[3]);
  not not_2 (not_2_out, in_1[4]);
  not not_3 (not_3_out, in_1[2]);
  not not_4 (not_4_out, in_1[1]);
  and addu (addu_out, in_1[5], not_2_out, not_1_out, not_3_out, not_4_out, in_1[0]);
  not not_5 (not_5_out, in_1[1]);
  not not_6 (not_6_out, in_1[2]);
  not not_7 (not_7_out, in_1[5]);
  and multu (multu_out, not_7_out, in_1[4], in_1[3], not_6_out, not_5_out, in_1[0]);
  not not_8 (not_8_out, in_1[4]);
  not not_9 (not_9_out, in_1[3]);
  not not_10 (not_10_out, in_1[1]);
  and \or  (or_out, in_1[5], not_8_out, not_9_out, in_1[2], not_10_out, in_1[0]);
  not not_11 (not_11_out, in_1[2]);
  not not_12 (not_12_out, in_1[4]);
  and slt (slt_out, in_1[5], not_12_out, in_1[3], not_11_out, in_1[1], not_16_out);
  or or_2 (Op1, addu_out, multu_out, or_out, slt_out, sra_out, sub_out);
  not not_13 (not_13_out, in_1[4]);
  not not_14 (not_14_out, in_1[3]);
  not not_15 (not_15_out, in_1[5]);
  not not_16 (not_16_out, in_1[0]);
  not not_17 (not_17_out, in_1[2]);
  and sra (sra_out, not_15_out, not_13_out, not_14_out, not_17_out, in_1[1], in_1[0]);
  not not_18 (not_18_out, in_1[2]);
  not not_19 (not_19_out, in_1[4]);
  not not_20 (not_20_out, in_1[3]);
  and sub (sub_out, in_1[5], not_19_out, not_20_out, not_18_out, in_1[1], not_21_out);
  not not_21 (not_21_out, in_1[0]);
endmodule

module RTypeOp2 (
  input  [5:0] in_1,
  output Op2
);

  wire add_out, addu_out, divu_out, not_1_out, not_2_out, not_3_out, not_4_out, not_5_out, not_6_out,
       not_7_out, not_8_out, not_9_out, not_10_out, not_11_out, not_12_out, not_13_out, not_14_out,
       not_15_out, not_16_out, not_17_out, sltu_out, sub_out;

  not not_1 (not_1_out, in_1[3]);
  not not_2 (not_2_out, in_1[2]);
  not not_3 (not_3_out, in_1[4]);
  not not_4 (not_4_out, in_1[1]);
  and add (add_out, in_1[5], not_3_out, not_1_out, not_2_out, not_4_out, not_6_out);
  not not_5 (not_5_out, in_1[1]);
  not not_6 (not_6_out, in_1[0]);
  not not_7 (not_7_out, in_1[4]);
  not not_8 (not_8_out, in_1[2]);
  not not_9 (not_9_out, in_1[3]);
  and addu (addu_out, in_1[5], not_7_out, not_9_out, not_8_out, not_5_out, in_1[0]);
  not not_10 (not_10_out, in_1[2]);
  not not_11 (not_11_out, in_1[5]);
  and divu (divu_out, not_11_out, in_1[4], in_1[3], not_10_out, in_1[1], in_1[0]);
  or or_1 (Op2, add_out, addu_out, divu_out, sltu_out, sub_out);
  not not_12 (not_12_out, in_1[4]);
  not not_13 (not_13_out, in_1[2]);
  and sltu (sltu_out, in_1[5], not_12_out, in_1[3], not_13_out, in_1[1], in_1[0]);
  not not_14 (not_14_out, in_1[3]);
  not not_15 (not_15_out, in_1[2]);
  not not_16 (not_16_out, in_1[4]);
  and sub (sub_out, in_1[5], not_16_out, not_14_out, not_15_out, in_1[1], not_17_out);
  not not_17 (not_17_out, in_1[0]);
endmodule

module RTypeOp3 (
  input  [5:0] in_1,
  output Op3
);

  wire and_out, not_1_out, not_2_out, not_3_out, not_4_out, not_5_out, not_6_out, not_7_out, not_8_out,
       not_9_out, not_10_out, not_11_out, not_12_out, not_13_out, not_14_out, not_15_out, or_out, slt_out,
       sltu_out, subu_out;

  not not_1 (not_1_out, in_1[4]);
  not not_2 (not_2_out, in_1[3]);
  not not_3 (not_3_out, in_1[1]);
  and \and  (and_out, in_1[5], not_1_out, not_2_out, in_1[2], not_3_out, not_6_out);
  not not_4 (not_4_out, in_1[1]);
  not not_5 (not_5_out, in_1[4]);
  not not_6 (not_6_out, in_1[0]);
  not not_7 (not_7_out, in_1[3]);
  and \or  (or_out, in_1[5], not_5_out, not_7_out, in_1[2], not_4_out, in_1[0]);
  not not_8 (not_8_out, in_1[2]);
  not not_9 (not_9_out, in_1[4]);
  and slt (slt_out, in_1[5], not_9_out, in_1[3], not_8_out, in_1[1], not_10_out);
  or or_2 (Op3, and_out, or_out, slt_out, sltu_out, subu_out);
  not not_10 (not_10_out, in_1[0]);
  not not_11 (not_11_out, in_1[4]);
  not not_12 (not_12_out, in_1[2]);
  and sltu (sltu_out, in_1[5], not_11_out, in_1[3], not_12_out, in_1[1], in_1[0]);
  not not_13 (not_13_out, in_1[3]);
  not not_14 (not_14_out, in_1[4]);
  not not_15 (not_15_out, in_1[2]);
  and subu (subu_out, in_1[5], not_14_out, not_13_out, not_15_out, in_1[1], in_1[0]);
endmodule

module ITypeOp0 (
  input  [5:0] in_1,
  output Operation_0
);

  wire addi_out, andi_out, lb_out, lw_out, not_1_out, not_2_out, not_3_out, not_4_out, not_5_out, not_6_out,
       not_7_out, not_8_out, not_9_out, not_10_out, not_11_out, not_12_out, not_13_out, not_14_out,
       not_15_out, not_16_out, not_17_out, not_18_out, not_19_out, not_20_out, not_21_out, not_22_out,
       not_23_out, not_24_out, not_25_out, not_26_out, not_27_out, not_28_out, not_29_out, not_30_out,
       not_31_out, not_32_out, not_33_out, sb_out, shw_out, slti_out, sw_out, swai_out;

  not not_1 (not_1_out, in_1[5]);
  not not_2 (not_2_out, in_1[1]);
  not not_3 (not_3_out, in_1[4]);
  not not_4 (not_4_out, in_1[2]);
  and addi (addi_out, not_1_out, not_3_out, in_1[3], not_4_out, not_2_out, not_6_out);
  not not_5 (not_5_out, in_1[4]);
  not not_6 (not_6_out, in_1[0]);
  not not_7 (not_7_out, in_1[5]);
  not not_8 (not_8_out, in_1[1]);
  and andi (andi_out, not_7_out, not_5_out, in_1[3], in_1[2], not_8_out, not_10_out);
  not not_9 (not_9_out, in_1[4]);
  not not_10 (not_10_out, in_1[0]);
  not not_11 (not_11_out, in_1[5]);
  not not_12 (not_12_out, in_1[2]);
  and slti (slti_out, not_11_out, not_9_out, in_1[3], not_12_out, in_1[1], not_17_out);
  not not_13 (not_13_out, in_1[2]);
  not not_14 (not_14_out, in_1[3]);
  not not_15 (not_15_out, in_1[4]);
  not not_16 (not_16_out, in_1[1]);
  not not_17 (not_17_out, in_1[0]);
  and lb (lb_out, in_1[5], not_15_out, not_14_out, not_13_out, not_16_out, not_21_out);
  not not_18 (not_18_out, in_1[4]);
  not not_19 (not_19_out, in_1[3]);
  not not_20 (not_20_out, in_1[2]);
  not not_21 (not_21_out, in_1[0]);
  and lw (lw_out, in_1[5], not_18_out, not_19_out, not_20_out, in_1[1], in_1[0]);
  or or_1 (Operation_0, addi_out, andi_out, slti_out, lb_out, lw_out, sb_out, shw_out, sw_out, swai_out);
  not not_22 (not_22_out, in_1[1]);
  not not_23 (not_23_out, in_1[4]);
  not not_24 (not_24_out, in_1[2]);
  and sb (sb_out, in_1[5], not_23_out, in_1[3], not_24_out, not_22_out, not_26_out);
  not not_25 (not_25_out, in_1[1]);
  not not_26 (not_26_out, in_1[0]);
  not not_27 (not_27_out, in_1[2]);
  not not_28 (not_28_out, in_1[4]);
  and shw (shw_out, in_1[5], not_28_out, in_1[3], not_27_out, not_25_out, in_1[0]);
  not not_29 (not_29_out, in_1[4]);
  not not_30 (not_30_out, in_1[2]);
  and sw (sw_out, in_1[5], not_29_out, in_1[3], not_30_out, in_1[1], in_1[0]);
  not not_31 (not_31_out, in_1[1]);
  not not_32 (not_32_out, in_1[4]);
  and swai (swai_out, in_1[5], not_32_out, in_1[3], in_1[2], not_31_out, not_33_out);
  not not_33 (not_33_out, in_1[0]);
endmodule

module ITypeOp1 (
  input  [5:0] in_1,
  output Operation_1
);

  wire addiu_out, lbu_out, lhwu_out, not_1_out, not_2_out, not_3_out, not_4_out, not_5_out, not_6_out,
       not_7_out, not_8_out, not_9_out, not_10_out, not_11_out, not_12_out, not_13_out, not_14_out,
       not_15_out, not_16_out, not_17_out, not_18_out, ori_out, slti_out;

  not not_1 (not_1_out, in_1[4]);
  not not_2 (not_2_out, in_1[5]);
  not not_3 (not_3_out, in_1[2]);
  not not_4 (not_4_out, in_1[1]);
  and addiu (addiu_out, not_2_out, not_1_out, in_1[3], not_3_out, not_4_out, in_1[0]);
  not not_5 (not_5_out, in_1[4]);
  not not_6 (not_6_out, in_1[1]);
  not not_7 (not_7_out, in_1[5]);
  and ori (ori_out, not_7_out, not_5_out, in_1[3], in_1[2], not_6_out, in_1[0]);
  not not_8 (not_8_out, in_1[5]);
  not not_9 (not_9_out, in_1[2]);
  not not_10 (not_10_out, in_1[4]);
  and slti (slti_out, not_8_out, not_10_out, in_1[3], not_9_out, in_1[1], not_12_out);
  or or_1 (Operation_1, addiu_out, ori_out, slti_out, lbu_out, lhwu_out);
  not not_11 (not_11_out, in_1[1]);
  not not_12 (not_12_out, in_1[0]);
  not not_13 (not_13_out, in_1[4]);
  not not_14 (not_14_out, in_1[3]);
  and lbu (lbu_out, in_1[5], not_13_out, not_14_out, in_1[2], not_11_out, not_18_out);
  not not_15 (not_15_out, in_1[3]);
  not not_16 (not_16_out, in_1[4]);
  not not_17 (not_17_out, in_1[1]);
  not not_18 (not_18_out, in_1[0]);
  and lhwu (lhwu_out, in_1[5], not_16_out, not_15_out, in_1[2], not_17_out, in_1[0]);
endmodule

module ITypeOp2 (
  input  [5:0] in_1,
  output Operation_2
);

  wire addi_out, addiu_out, lb_out, lbu_out, lhwu_out, lw_out, not_1_out, not_2_out, not_3_out, not_4_out,
       not_5_out, not_6_out, not_7_out, not_8_out, not_9_out, not_10_out, not_11_out, not_12_out, not_13_out,
       not_14_out, not_15_out, not_16_out, not_17_out, not_18_out, not_19_out, not_20_out, not_21_out,
       not_22_out, not_23_out, not_24_out, not_25_out, not_26_out, not_27_out, not_28_out, not_29_out,
       not_30_out, not_31_out, not_32_out, not_33_out, not_34_out, not_35_out, not_36_out, sb_out, shw_out,
       sw_out, swai_out;

  not not_1 (not_1_out, in_1[5]);
  not not_2 (not_2_out, in_1[1]);
  not not_3 (not_3_out, in_1[4]);
  not not_4 (not_4_out, in_1[2]);
  and addi (addi_out, not_1_out, not_3_out, in_1[3], not_4_out, not_2_out, not_8_out);
  not not_5 (not_5_out, in_1[1]);
  not not_6 (not_6_out, in_1[5]);
  not not_7 (not_7_out, in_1[2]);
  not not_8 (not_8_out, in_1[0]);
  not not_9 (not_9_out, in_1[4]);
  and addiu (addiu_out, not_6_out, not_9_out, in_1[3], not_7_out, not_5_out, in_1[0]);
  not not_10 (not_10_out, in_1[3]);
  not not_11 (not_11_out, in_1[4]);
  not not_12 (not_12_out, in_1[2]);
  not not_13 (not_13_out, in_1[1]);
  and lb (lb_out, in_1[5], not_11_out, not_10_out, not_12_out, not_13_out, not_16_out);
  not not_14 (not_14_out, in_1[1]);
  not not_15 (not_15_out, in_1[3]);
  not not_16 (not_16_out, in_1[0]);
  not not_17 (not_17_out, in_1[4]);
  and lbu (lbu_out, in_1[5], not_17_out, not_15_out, in_1[2], not_14_out, not_18_out);
  not not_18 (not_18_out, in_1[0]);
  not not_19 (not_19_out, in_1[1]);
  not not_20 (not_20_out, in_1[4]);
  not not_21 (not_21_out, in_1[3]);
  and lhwu (lhwu_out, in_1[5], not_20_out, not_21_out, in_1[2], not_19_out, in_1[0]);
  not not_22 (not_22_out, in_1[2]);
  not not_23 (not_23_out, in_1[4]);
  not not_24 (not_24_out, in_1[3]);
  and lw (lw_out, in_1[5], not_23_out, not_24_out, not_22_out, in_1[1], in_1[0]);
  or or_1 (Operation_2, addi_out, addiu_out, lb_out, lbu_out, lhwu_out, lw_out, sb_out, shw_out, sw_out, swai_out);
  not not_25 (not_25_out, in_1[1]);
  not not_26 (not_26_out, in_1[2]);
  not not_27 (not_27_out, in_1[4]);
  and sb (sb_out, in_1[5], not_27_out, in_1[3], not_26_out, not_25_out, not_30_out);
  not not_28 (not_28_out, in_1[4]);
  not not_29 (not_29_out, in_1[1]);
  not not_30 (not_30_out, in_1[0]);
  not not_31 (not_31_out, in_1[2]);
  and shw (shw_out, in_1[5], not_28_out, in_1[3], not_31_out, not_29_out, in_1[0]);
  not not_32 (not_32_out, in_1[2]);
  not not_33 (not_33_out, in_1[4]);
  and sw (sw_out, in_1[5], not_33_out, in_1[3], not_32_out, in_1[1], in_1[0]);
  not not_34 (not_34_out, in_1[1]);
  not not_35 (not_35_out, in_1[4]);
  and swai (swai_out, in_1[5], not_35_out, in_1[3], in_1[2], not_34_out, not_36_out);
  not not_36 (not_36_out, in_1[0]);
endmodule

module ITypeOp3 (
  input  [5:0] in_1,
  output Operation_3
);

  wire andi_out, not_1_out, not_2_out, not_3_out, not_4_out, not_5_out, not_6_out, not_7_out, not_8_out,
       not_9_out, not_10_out, not_11_out, ori_out, slti_out;

  not not_1 (not_1_out, in_1[1]);
  not not_2 (not_2_out, in_1[4]);
  not not_3 (not_3_out, in_1[5]);
  and andi (andi_out, not_3_out, not_2_out, in_1[3], in_1[2], not_1_out, not_4_out);
  not not_4 (not_4_out, in_1[0]);
  not not_5 (not_5_out, in_1[4]);
  not not_6 (not_6_out, in_1[5]);
  not not_7 (not_7_out, in_1[1]);
  and ori (ori_out, not_6_out, not_5_out, in_1[3], in_1[2], not_7_out, in_1[0]);
  or or_1 (Operation_3, andi_out, ori_out, slti_out);
  not not_8 (not_8_out, in_1[4]);
  not not_9 (not_9_out, in_1[5]);
  not not_10 (not_10_out, in_1[2]);
  and slti (slti_out, not_9_out, not_8_out, in_1[3], not_10_out, in_1[1], not_11_out);
  not not_11 (not_11_out, in_1[0]);
endmodule

module ImmediateExtender (
  input  [15:0] ImmVal,
  input  [5:0] opcode,
  output [31:0] ExtVal
);

  wire comparator_1_eq, comparator_2_eq, comparator_3_eq, or_1_out;
  wire [31:0] bit_extender_1_out, bit_extender_2_out, multiplexer_1_out, shifter_1_out;

  assign bit_extender_1_out = {{16{ImmVal[15]}}, ImmVal};  // Bit_Extender bit_extender_1
  assign bit_extender_2_out = {{16{1'b0}}, ImmVal};  // Bit_Extender bit_extender_2
  Shifter #(.width(32)) shifter_1 (.in(bit_extender_2_out), .\dist (5'b10000), .out(shifter_1_out));
  Comparator #(.width(6), .mode("unsigned")) comparator_1 (
    .a(opcode), .b(6'b001100), .eq(comparator_1_eq));  // open: gt, lt
  Comparator #(.width(6), .mode("unsigned")) comparator_2 (
    .a(opcode), .b(6'b001101), .eq(comparator_2_eq));  // open: gt, lt
  Multiplexer #(.width(32)) multiplexer_1 (
    .in0(bit_extender_1_out), .in1(bit_extender_2_out), .out(multiplexer_1_out), .sel(or_1_out));  // open: en
  or or_1 (or_1_out, comparator_1_eq, comparator_2_eq);
  Comparator #(.width(6), .mode("unsigned")) comparator_3 (
    .a(opcode), .b(6'b001111), .eq(comparator_3_eq));  // open: gt, lt
  Multiplexer #(.width(32)) multiplexer_2 (
    .in0(multiplexer_1_out), .in1(shifter_1_out), .out(ExtVal), .sel(comparator_3_eq));  // open: en

  // Notes on the sheet:
  //   andi
  //   ori
  //   lui
endmodule

module multu_or_divu (
  input  [5:0] funct,
  input  [5:0] opcode,
  output multu_or_divu
);

  wire comparator_1_eq, comparator_2_eq, comparator_3_eq, or_1_out;

  Comparator #(.width(6), .mode("unsigned")) comparator_1 (
    .a(funct), .b(6'b011001), .eq(comparator_1_eq));  // open: gt, lt
  Comparator #(.width(6), .mode("unsigned")) comparator_2 (
    .a(funct), .b(6'b011011), .eq(comparator_2_eq));  // open: gt, lt
  Comparator #(.width(6), .mode("unsigned")) comparator_3 (
    .a(opcode), .b({6{1'b0}}), .eq(comparator_3_eq));  // open: gt, lt
  or or_1 (or_1_out, comparator_1_eq, comparator_2_eq);
  and and_1 (multu_or_divu, or_1_out, comparator_3_eq);

  // Notes on the sheet:
  //   multu
  //   divu
endmodule

module mfhi_control (
  input  [5:0] opcode,
  input  [5:0] funct,
  output mfhi
);

  wire comparator_1_eq, comparator_2_eq;

  Comparator #(.width(6), .mode("unsigned")) comparator_1 (
    .a({6{1'b0}}), .b(opcode), .eq(comparator_1_eq));  // open: gt, lt
  Comparator #(.width(6), .mode("unsigned")) comparator_2 (
    .a(6'b010000), .b(funct), .eq(comparator_2_eq));  // open: gt, lt
  and and_1 (mfhi, comparator_1_eq, comparator_2_eq);
endmodule

module mflo_control (
  input  [5:0] opcode,
  input  [5:0] funct,
  output mflo
);

  wire comparator_1_eq, comparator_2_eq;

  Comparator #(.width(6), .mode("unsigned")) comparator_1 (
    .a({6{1'b0}}), .b(opcode), .eq(comparator_1_eq));  // open: gt, lt
  Comparator #(.width(6), .mode("unsigned")) comparator_2 (
    .a(6'b010010), .b(funct), .eq(comparator_2_eq));  // open: gt, lt
  and and_1 (mflo, comparator_1_eq, comparator_2_eq);
endmodule

module jr_control (
  input  [5:0] opcode,
  input  [5:0] funct,
  output jr
);

  wire comparator_1_eq, comparator_2_eq;

  Comparator #(.width(6), .mode("unsigned")) comparator_1 (
    .a({6{1'b0}}), .b(opcode), .eq(comparator_1_eq));  // open: gt, lt
  Comparator #(.width(6), .mode("unsigned")) comparator_2 (
    .a(6'b001000), .b(funct), .eq(comparator_2_eq));  // open: gt, lt
  and and_1 (jr, comparator_1_eq, comparator_2_eq);
endmodule

module shift_control (
  input  [5:0] opcode,
  input  [5:0] funct,
  output shift_control
);

  wire comparator_1_eq, comparator_2_eq, comparator_3_eq, comparator_4_eq, or_1_out;

  Comparator #(.width(6), .mode("unsigned")) comparator_1 (
    .a(opcode), .b({6{1'b0}}), .eq(comparator_1_eq));  // open: gt, lt
  Comparator #(.width(6), .mode("unsigned")) comparator_2 (
    .a(funct), .b({6{1'b0}}), .eq(comparator_2_eq));  // open: gt, lt
  Comparator #(.width(6), .mode("unsigned")) comparator_3 (
    .a(funct), .b(6'b000010), .eq(comparator_3_eq));  // open: gt, lt
  Comparator #(.width(6), .mode("unsigned")) comparator_4 (
    .a(funct), .b(6'b000011), .eq(comparator_4_eq));  // open: gt, lt
  or or_1 (or_1_out, comparator_2_eq, comparator_3_eq, comparator_4_eq);
  and and_1 (shift_control, comparator_1_eq, or_1_out);
endmodule
