// Logisim project regfile.circ as structural Verilog: 2 circuits, main circuit main
module main (
  input  [4:0] Read_Register_1,
  input  [4:0] Read_Register_2,
  input  [4:0] Write_Register,
  input  [31:0] Write_Data,
  input  Write_Enable,
  input  Clock,
  output [31:0] s0_Value,
  output [31:0] s1_Value,
  output [31:0] s2_Value,
  output [31:0] ra_Value,
  output [31:0] Read_Data_1,
  output [31:0] Read_Data_2
);

  wire [31:0] augmented_register_1_read_1_out, augmented_register_1_read_2_out,
       augmented_register_2_read_1_out, augmented_register_2_read_2_out, augmented_register_3_read_1_out,
       augmented_register_3_read_2_out, augmented_register_4_read_1_out, augmented_register_4_read_2_out,
       augmented_register_5_read_1_out, augmented_register_5_read_2_out, augmented_register_6_read_1_out,
       augmented_register_6_read_2_out, augmented_register_7_read_1_out, augmented_register_7_read_2_out,
       augmented_register_8_read_1_out, augmented_register_8_read_2_out, augmented_register_9_read_1_out,
       augmented_register_9_read_2_out, augmented_register_10_read_1_out, augmented_register_10_read_2_out,
       augmented_register_11_read_1_out, augmented_register_11_read_2_out, augmented_register_12_read_1_out,
       augmented_register_12_read_2_out, augmented_register_13_read_1_out, augmented_register_13_read_2_out,
       augmented_register_14_read_1_out, augmented_register_14_read_2_out, augmented_register_15_read_1_out,
       augmented_register_15_read_2_out, augmented_register_16_read_1_out, augmented_register_16_read_2_out,
       augmented_register_17_read_1_out, augmented_register_17_read_2_out, augmented_register_18_read_1_out,
       augmented_register_18_read_2_out, augmented_register_19_read_1_out, augmented_register_19_read_2_out,
       augmented_register_20_read_1_out, augmented_register_20_read_2_out, augmented_register_21_read_1_out,
       augmented_register_21_read_2_out, augmented_register_22_read_1_out, augmented_register_22_read_2_out,
       augmented_register_23_read_1_out, augmented_register_23_read_2_out, augmented_register_24_read_1_out,
       augmented_register_24_read_2_out, augmented_register_25_read_1_out, augmented_register_25_read_2_out,
       augmented_register_26_read_1_out, augmented_register_26_read_2_out, augmented_register_27_read_1_out,
       augmented_register_27_read_2_out, augmented_register_28_read_1_out, augmented_register_28_read_2_out,
       augmented_register_29_read_1_out, augmented_register_29_read_2_out, augmented_register_30_read_1_out,
       augmented_register_30_read_2_out, augmented_register_31_read_1_out, augmented_register_31_read_2_out;

  augmented_register augmented_register_1 (
    .write_data(Write_Data), .write_reg(Write_Register), .read_reg1(Read_Register_1), .reg_num({5{1'b0}}),
    .read_reg2(Read_Register_2), .read_1_out(augmented_register_1_read_1_out),
    .read_2_out(augmented_register_1_read_2_out), .CLK(Clock));  // open: read_1_in, data, read_2_in, enable_write
  augmented_register augmented_register_2 (
    .write_data(Write_Data), .write_reg(Write_Register), .read_1_in(augmented_register_29_read_1_out),
    .read_reg1(Read_Register_1), .reg_num(5'b01000), .read_reg2(Read_Register_2),
    .read_1_out(augmented_register_2_read_1_out), .read_2_out(augmented_register_2_read_2_out),
    .read_2_in(augmented_register_29_read_2_out), .CLK(Clock), .enable_write(Write_Enable));  // open: data
  augmented_register augmented_register_3 (
    .write_data(Write_Data), .write_reg(Write_Register), .read_1_in(augmented_register_30_read_1_out),
    .read_reg1(Read_Register_1), .reg_num(5'b10000), .read_reg2(Read_Register_2), .data(s0_Value),
    .read_1_out(augmented_register_3_read_1_out), .read_2_out(augmented_register_3_read_2_out),
    .read_2_in(augmented_register_30_read_2_out), .CLK(Clock), .enable_write(Write_Enable));
  augmented_register augmented_register_4 (
    .write_data(Write_Data), .write_reg(Write_Register), .read_1_in(augmented_register_31_read_1_out),
    .read_reg1(Read_Register_1), .reg_num(5'b11000), .read_reg2(Read_Register_2),
    .read_1_out(augmented_register_4_read_1_out), .read_2_out(augmented_register_4_read_2_out),
    .read_2_in(augmented_register_31_read_2_out), .CLK(Clock), .enable_write(Write_Enable));  // open: data
  augmented_register augmented_register_5 (
    .write_data(Write_Data), .write_reg(Write_Register), .read_1_in(augmented_register_1_read_1_out),
    .read_reg1(Read_Register_1), .reg_num(5'b00001), .read_reg2(Read_Register_2),
    .read_1_out(augmented_register_5_read_1_out), .read_2_out(augmented_register_5_read_2_out),
    .read_2_in(augmented_register_1_read_2_out), .CLK(Clock), .enable_write(Write_Enable));  // open: data
  augmented_register augmented_register_6 (
    .write_data(Write_Data), .write_reg(Write_Register), .read_1_in(augmented_register_2_read_1_out),
    .read_reg1(Read_Register_1), .reg_num(5'b01001), .read_reg2(Read_Register_2),
    .read_1_out(augmented_register_6_read_1_out), .read_2_out(augmented_register_6_read_2_out),
    .read_2_in(augmented_register_2_read_2_out), .CLK(Clock), .enable_write(Write_Enable));  // open: data
  augmented_register augmented_register_7 (
    .write_data(Write_Data), .write_reg(Write_Register), .read_1_in(augmented_register_3_read_1_out),
    .read_reg1(Read_Register_1), .reg_num(5'b10001), .read_reg2(Read_Register_2), .data(s1_Value),
    .read_1_out(augmented_register_7_read_1_out), .read_2_out(augmented_register_7_read_2_out),
    .read_2_in(augmented_register_3_read_2_out), .CLK(Clock), .enable_write(Write_Enable));
  augmented_register augmented_register_8 (
    .write_data(Write_Data), .write_reg(Write_Register), .read_1_in(augmented_register_4_read_1_out),
    .read_reg1(Read_Register_1), .reg_num(5'b11001), .read_reg2(Read_Register_2),
    .read_1_out(augmented_register_8_read_1_out), .read_2_out(augmented_register_8_read_2_out),
    .read_2_in(augmented_register_4_read_2_out), .CLK(Clock), .enable_write(Write_Enable));  // open: data
  augmented_register augmented_register_9 (
    .write_data(Write_Data), .write_reg(Write_Register), .read_1_in(augmented_register_5_read_1_out),
    .read_reg1(Read_Register_1), .reg_num(5'b00010), .read_reg2(Read_Register_2),
    .read_1_out(augmented_register_9_read_1_out), .read_2_out(augmented_register_9_read_2_out),
    .read_2_in(augmented_register_5_read_2_out), .CLK(Clock), .enable_write(Write_Enable));  // open: data
  augmented_register augmented_register_10 (
    .write_data(Write_Data), .write_reg(Write_Register), .read_1_in(augmented_register_6_read_1_out),
    .read_reg1(Read_Register_1), .reg_num(5'b01010), .read_reg2(Read_Register_2),
    .read_1_out(augmented_register_10_read_1_out), .read_2_out(augmented_register_10_read_2_out),
    .read_2_in(augmented_register_6_read_2_out), .CLK(Clock), .enable_write(Write_Enable));  // open: data
  augmented_register augmented_register_11 (
    .write_data(Write_Data), .write_reg(Write_Register), .read_1_in(augmented_register_7_read_1_out),
    .read_reg1(Read_Register_1), .reg_num(5'b10010), .read_reg2(Read_Register_2), .data(s2_Value),
    .read_1_out(augmented_register_11_read_1_out), .read_2_out(augmented_register_11_read_2_out),
    .read_2_in(augmented_register_7_read_2_out), .CLK(Clock), .enable_write(Write_Enable));
  augmented_register augmented_register_12 (
    .write_data(Write_Data), .write_reg(Write_Register), .read_1_in(augmented_register_8_read_1_out),
    .read_reg1(Read_Register_1), .reg_num(5'b11010), .read_reg2(Read_Register_2),
    .read_1_out(augmented_register_12_read_1_out), .read_2_out(augmented_register_12_read_2_out),
    .read_2_in(augmented_register_8_read_2_out), .CLK(Clock), .enable_write(Write_Enable));  // open: data
  augmented_register augmented_register_13 (
    .write_data(Write_Data), .write_reg(Write_Register), .read_1_in(augmented_register_9_read_1_out),
    .read_reg1(Read_Register_1), .reg_num(5'b00011), .read_reg2(Read_Register_2),
    .read_1_out(augmented_register_13_read_1_out), .read_2_out(augmented_register_13_read_2_out),
    .read_2_in(augmented_register_9_read_2_out), .CLK(Clock), .enable_write(Write_Enable));  // open: data
  augmented_register augmented_register_14 (
    .write_data(Write_Data), .write_reg(Write_Register), .read_1_in(augmented_register_10_read_1_out),
    .read_reg1(Read_Register_1), .reg_num(5'b01011), .read_reg2(Read_Register_2),
    .read_1_out(augmented_register_14_read_1_out), .read_2_out(augmented_register_14_read_2_out),
    .read_2_in(augmented_register_10_read_2_out), .CLK(Clock), .enable_write(Write_Enable));  // open: data
  augmented_register augmented_register_15 (
    .write_data(Write_Data), .write_reg(Write_Register), .read_1_in(augmented_register_11_read_1_out),
    .read_reg1(Read_Register_1), .reg_num(5'b10011), .read_reg2(Read_Register_2),
    .read_1_out(augmented_register_15_read_1_out), .read_2_out(augmented_register_15_read_2_out),
    .read_2_in(augmented_register_11_read_2_out), .CLK(Clock), .enable_write(Write_Enable));  // open: data
  augmented_register augmented_register_16 (
    .write_data(Write_Data), .write_reg(Write_Register), .read_1_in(augmented_register_12_read_1_out),
    .read_reg1(Read_Register_1), .reg_num(5'b11011), .read_reg2(Read_Register_2),
    .read_1_out(augmented_register_16_read_1_out), .read_2_out(augmented_register_16_read_2_out),
    .read_2_in(augmented_register_12_read_2_out), .CLK(Clock), .enable_write(Write_Enable));  // open: data
  augmented_register augmented_register_17 (
    .write_data(Write_Data), .write_reg(Write_Register), .read_1_in(augmented_register_13_read_1_out),
    .read_reg1(Read_Register_1), .reg_num(5'b00100), .read_reg2(Read_Register_2),
    .read_1_out(augmented_register_17_read_1_out), .read_2_out(augmented_register_17_read_2_out),
    .read_2_in(augmented_register_13_read_2_out), .CLK(Clock), .enable_write(Write_Enable));  // open: data
  augmented_register augmented_register_18 (
    .write_data(Write_Data), .write_reg(Write_Register), .read_1_in(augmented_register_14_read_1_out),
    .read_reg1(Read_Register_1), .reg_num(5'b01100), .read_reg2(Read_Register_2),
    .read_1_out(augmented_register_18_read_1_out), .read_2_out(augmented_register_18_read_2_out),
    .read_2_in(augmented_register_14_read_2_out), .CLK(Clock), .enable_write(Write_Enable));  // open: data
  augmented_register augmented_register_19 (
    .write_data(Write_Data), .write_reg(Write_Register), .read_1_in(augmented_register_15_read_1_out),
    .read_reg1(Read_Register_1), .reg_num(5'b10100), .read_reg2(Read_Register_2),
    .read_1_out(augmented_register_19_read_1_out), .read_2_out(augmented_register_19_read_2_out),
    .read_2_in(augmented_register_15_read_2_out), .CLK(Clock), .enable_write(Write_Enable));  // open: data
  augmented_register augmented_register_20 (
    .write_data(Write_Data), .write_reg(Write_Register), .read_1_in(augmented_register_16_read_1_out),
    .read_reg1(Read_Register_1), .reg_num(5'b11100), .read_reg2(Read_Register_2),
    .read_1_out(augmented_register_20_read_1_out), .read_2_out(augmented_register_20_read_2_out),
    .read_2_in(augmented_register_16_read_2_out), .CLK(Clock), .enable_write(Write_Enable));  // open: data
  augmented_register augmented_register_21 (
    .write_data(Write_Data), .write_reg(Write_Register), .read_1_in(augmented_register_17_read_1_out),
    .read_reg1(Read_Register_1), .reg_num(5'b00101), .read_reg2(Read_Register_2),
    .read_1_out(augmented_register_21_read_1_out), .read_2_out(augmented_register_21_read_2_out),
    .read_2_in(augmented_register_17_read_2_out), .CLK(Clock), .enable_write(Write_Enable));  // open: data
  augmented_register augmented_register_22 (
    .write_data(Write_Data), .write_reg(Write_Register), .read_1_in(augmented_register_18_read_1_out),
    .read_reg1(Read_Register_1), .reg_num(5'b01101), .read_reg2(Read_Register_2),
    .read_1_out(augmented_register_22_read_1_out), .read_2_out(augmented_register_22_read_2_out),
    .read_2_in(augmented_register_18_read_2_out), .CLK(Clock), .enable_write(Write_Enable));  // open: data
  augmented_register augmented_register_23 (
    .write_data(Write_Data), .write_reg(Write_Register), .read_1_in(augmented_register_19_read_1_out),
    .read_reg1(Read_Register_1), .reg_num(5'b10101), .read_reg2(Read_Register_2),
    .read_1_out(augmented_register_23_read_1_out), .read_2_out(augmented_register_23_read_2_out),
    .read_2_in(augmented_register_19_read_2_out), .CLK(Clock), .enable_write(Write_Enable));  // open: data
  augmented_register augmented_register_24 (
    .write_data(Write_Data), .write_reg(Write_Register), .read_1_in(augmented_register_20_read_1_out),
    .read_reg1(Read_Register_1), .reg_num(5'b11101), .read_reg2(Read_Register_2),
    .read_1_out(augmented_register_24_read_1_out), .read_2_out(augmented_register_24_read_2_out),
    .read_2_in(augmented_register_20_read_2_out), .CLK(Clock), .enable_write(Write_Enable));  // open: data
  augmented_register augmented_register_25 (
    .write_data(Write_Data), .write_reg(Write_Register), .read_1_in(augmented_register_21_read_1_out),
    .read_reg1(Read_Register_1), .reg_num(5'b00110), .read_reg2(Read_Register_2),
    .read_1_out(augmented_register_25_read_1_out), .read_2_out(augmented_register_25_read_2_out),
    .read_2_in(augmented_register_21_read_2_out), .CLK(Clock), .enable_write(Write_Enable));  // open: data
  augmented_register augmented_register_26 (
    .write_data(Write_Data), .write_reg(Write_Register), .read_1_in(augmented_register_22_read_1_out),
    .read_reg1(Read_Register_1), .reg_num(5'b01110), .read_reg2(Read_Register_2),
    .read_1_out(augmented_register_26_read_1_out), .read_2_out(augmented_register_26_read_2_out),
    .read_2_in(augmented_register_22_read_2_out), .CLK(Clock), .enable_write(Write_Enable));  // open: data
  augmented_register augmented_register_27 (
    .write_data(Write_Data), .write_reg(Write_Register), .read_1_in(augmented_register_23_read_1_out),
    .read_reg1(Read_Register_1), .reg_num(5'b10110), .read_reg2(Read_Register_2),
    .read_1_out(augmented_register_27_read_1_out), .read_2_out(augmented_register_27_read_2_out),
    .read_2_in(augmented_register_23_read_2_out), .CLK(Clock), .enable_write(Write_Enable));  // open: data
  augmented_register augmented_register_28 (
    .write_data(Write_Data), .write_reg(Write_Register), .read_1_in(augmented_register_24_read_1_out),
    .read_reg1(Read_Register_1), .reg_num(5'b11110), .read_reg2(Read_Register_2),
    .read_1_out(augmented_register_28_read_1_out), .read_2_out(augmented_register_28_read_2_out),
    .read_2_in(augmented_register_24_read_2_out), .CLK(Clock), .enable_write(Write_Enable));  // open: data
  augmented_register augmented_register_29 (
    .write_data(Write_Data), .write_reg(Write_Register), .read_1_in(augmented_register_25_read_1_out),
    .read_reg1(Read_Register_1), .reg_num(5'b00111), .read_reg2(Read_Register_2),
    .read_1_out(augmented_register_29_read_1_out), .read_2_out(augmented_register_29_read_2_out),
    .read_2_in(augmented_register_25_read_2_out), .CLK(Clock), .enable_write(Write_Enable));  // open: data
  augmented_register augmented_register_30 (
    .write_data(Write_Data), .write_reg(Write_Register), .read_1_in(augmented_register_26_read_1_out),
    .read_reg1(Read_Register_1), .reg_num(5'b01111), .read_reg2(Read_Register_2),
    .read_1_out(augmented_register_30_read_1_out), .read_2_out(augmented_register_30_read_2_out),
    .read_2_in(augmented_register_26_read_2_out), .CLK(Clock), .enable_write(Write_Enable));  // open: data
  augmented_register augmented_register_31 (
    .write_data(Write_Data), .write_reg(Write_Register), .read_1_in(augmented_register_27_read_1_out),
    .read_reg1(Read_Register_1), .reg_num(5'b10111), .read_reg2(Read_Register_2),
    .read_1_out(augmented_register_31_read_1_out), .read_2_out(augmented_register_31_read_2_out),
    .read_2_in(augmented_register_27_read_2_out), .CLK(Clock), .enable_write(Write_Enable));  // open: data
  augmented_register augmented_register_32 (
    .write_data(Write_Data), .write_reg(Write_Register), .read_1_in(augmented_register_28_read_1_out),
    .read_reg1(Read_Register_1), .reg_num({5{1'b1}}), .read_reg2(Read_Register_2), .data(ra_Value),
    .read_1_out(Read_Data_1), .read_2_out(Read_Data_2), .read_2_in(augmented_register_28_read_2_out),
    .CLK(Clock), .enable_write(Write_Enable));

  // Other names for the same wires on the sheet: clk = Clock; write_en = Write_Enable;
  //   write_reg[4:0] = Write_Register; read_reg1[4:0] = Read_Register_1; read_reg2[4:0] = Read_Register_2;
  //   ra_val[31:0] = ra_Value; read_data1[31:0] = Read_Data_1; read_data2[31:0] = Read_Data_2;
  //   s0_val[31:0] = s0_Value; s1_val[31:0] = s1_Value; s2_val[31:0] = s2_Value

  // Notes on the sheet:
  //   INPUTS to your circuit
  //   DON'T CHANGE THE LOCATIONS OF THE INPUTS AND OUTPUTS!
  //   These are DEBUG/TEST outputs from your circuit.
  //   OUTPUTS from your circuit
endmodule

module augmented_register (
  input  [31:0] write_data,
  input  CLK,
  input  [4:0] write_reg,
  input  enable_write,
  input  [31:0] read_1_in,
  input  [4:0] read_reg1,
  input  [4:0] reg_num,
  input  [4:0] read_reg2,
  input  [31:0] read_2_in,
  output [31:0] data,
  output [31:0] read_1_out,
  output [31:0] read_2_out
);

  wire and_1_out, comparator_1_eq, comparator_2_eq, comparator_3_eq;
  wire [31:0] multiplexer_1_out;

  Comparator #(.width(5)) comparator_1 (.a(write_reg), .b(reg_num), .eq(comparator_1_eq));  // open: gt, lt
  and and_1 (and_1_out, comparator_1_eq, enable_write);
  Multiplexer #(.width(32)) multiplexer_1 (
    .in0(data), .in1(write_data), .out(multiplexer_1_out), .sel(and_1_out));  // open: en
  Comparator #(.width(5)) comparator_2 (.a(read_reg1), .b(reg_num), .eq(comparator_2_eq));  // open: gt, lt
  Comparator #(.width(5)) comparator_3 (.a(reg_num), .b(read_reg2), .eq(comparator_3_eq));  // open: gt, lt
  Register #(.width(32)) register_1 (.D(multiplexer_1_out), .Q(data), .clk(CLK));  // open: en, clr
  Multiplexer #(.width(32)) multiplexer_2 (
    .in0(read_1_in), .in1(data), .out(read_1_out), .sel(comparator_2_eq));  // open: en
  Multiplexer #(.width(32)) multiplexer_3 (
    .in0(read_2_in), .in1(data), .out(read_2_out), .sel(comparator_3_eq));  // open: en

  // Other names for the same wires on the sheet: out1[31:0] = read_1_out; out2[31:0] = read_2_out
endmodule
